# Fritzing sketch Circuit (saved by Fritzing 0.9.3b)
breadboards: 1

parts:
  IC1 = ULN2803A [package=THT]
  IC2 = ULN2803A [package=THT]  # not connected
  Raspberry_Pi_1 = Raspberry Pi 3 [part_number=RPI-3-V1.2]
  Power_plug_12_V = Power plug
  PIR_Motion_Sensor_Upstairs = PIR sensor
  PIR_Motion_Sensor_Downstairs = PIR sensor
  LED_strip_/_stair_#1 = LTE-302 [package=lte-302]
  LED_strip_/_stair_#2 = LTE-302 [package=lte-302]
  LED_strip_/_stair_#3 = LTE-302 [package=lte-302]
  LED_strip_/_stair_#4 = LTE-302 [package=lte-302]
  LED_strip_/_stair_#X = LTE-302 [package=lte-302]

nets:
  N1: IC1.In_1, Raspberry_Pi_1.GPIO6
  N2: IC1.In_7, Raspberry_Pi_1.GPIO5
  N3: IC1.In_8, Raspberry_Pi_1.GPIO4
  GND: IC1.0V, Raspberry_Pi_1.GND, Power_plug_12_V.GND, PIR_Motion_Sensor_Upstairs.GND, PIR_Motion_Sensor_Downstairs.GND
  N4: IC1.Out_8, LED_strip_/_stair_#1.A
  N5: IC1.Out_7, LED_strip_/_stair_#2.A
  N6: IC1.Out_1, LED_strip_/_stair_#3.A
  VDD: Raspberry_Pi_1.GPIO24, Raspberry_Pi_1.5V, PIR_Motion_Sensor_Upstairs.VDD, PIR_Motion_Sensor_Upstairs.SIG, PIR_Motion_Sensor_Downstairs.VDD
  N7: Raspberry_Pi_1.GPIO23, PIR_Motion_Sensor_Downstairs.SIG
  N8: Power_plug_12_V.VCC, LED_strip_/_stair_#1.C, LED_strip_/_stair_#2.C, LED_strip_/_stair_#3.C, LED_strip_/_stair_#4.C, LED_strip_/_stair_#X.C
